# Fritzing sketch lehmann_martin (saved by Fritzing 0.8.3b)
breadboards: 1

parts:
  J1 = female pin header, 1 pin [form="♀ (female)"]
  J2 = female pin header, 1 pin [form="♀ (female)"]
  J3 = female pin header, 1 pin [form="♀ (female)"]
  J4 = female pin header, 1 pin [form="♀ (female)"]
  J5 = female pin header, 1 pin [form="♀ (female)"]
  J6 = female pin header, 1 pin [form="♀ (female)"]
  J7 = female pin header, 1 pin [form="♀ (female)"]
  J8 = female pin header, 1 pin [form="♀ (female)"]
  J9 = female pin header, 1 pin [form="♀ (female)"]
  J10 = female pin header, 1 pin [form="♀ (female)"]  # not connected
  J11 = female pin header, 1 pin [form="♀ (female)"]  # not connected
  J12 = female pin header, 1 pin [form="♀ (female)"]  # not connected
  J13 = female pin header, 1 pin [form="♀ (female)"]  # not connected
  J14 = female pin header, 1 pin [form="♀ (female)"]
  J18 = female pin header, 1 pin [form="♀ (female)"]
  J16 = female pin header, 1 pin [form="♀ (female)"]
  J15 = female pin header, 1 pin [form="♀ (female)"]
  J17 = female pin header, 1 pin [form="♀ (female)"]
  Part1 = Arduino Uno (Rev3)

nets:
  N1: J1.pin1, J18.pin1, Part1.5V
  N2: J2.pin1, J17.pin1, Part1.GND
  N3: J3.pin1, Part1.ICSP_SCK, Part1.D13/SCK
  N4: J4.pin1, Part1.ICSP_MOSI, Part1.D11_PWM/MOSI
  N5: J5.pin1, Part1.D9_PWM
  N6: J6.pin1, Part1.D8
  N7: J7.pin1, Part1.D10_PWM/SS
  N8: J8.pin1, Part1.D4
  N9: J9.pin1, Part1.ICSP_MISO, Part1.D12/MISO
  N10: J14.pin1, Part1.A4/SDA
  N11: J16.pin1, Part1.A5/SCL
  N12: J15.pin1, Part1.A3

notes:
  VCC
  <screen>
  joystick
  SW
